// Logisim project control-logic.circ as structural Verilog: 1 circuit, main circuit control_logic
module control_logic (
  input  [31:0] inst,
  input  BrEq,
  input  BrLt,
  input  [3:0] in_4,
  output PCSel,
  output RegWEn,
  output [2:0] ImmSel,
  output BrUn,
  output ASel,
  output BSel,
  output [3:0] ALUSel,
  output MemRW,
  output [1:0] WBSel,
  output CSRSel,
  output CSRWen
);

  wire and_21_out, is_and, is_andi, is_I_type, is_lui, is_mul, is_mulh, is_mulhu, is_or, is_ori,
       is_SB_or_is_jalr, is_sll, is_slli, is_slt, is_slti, is_sra, is_srai, is_srl, is_srli, is_sub, is_UJ,
       is_UJ_type, is_xor, is_xori, or_6_out, or_8_out;
  wire [2:0] bit_extender_1_out;

  assign bit_extender_1_out = {{2{1'b0}}, inst[3]};  // Bit_Extender bit_extender_1
  and and_1 (is_sll, inst[12], BSel);
  and and_2 (is_mulh, inst[12], inst[25], BSel);
  and and_3 (is_srl, inst[14], inst[12], BSel);
  and and_4 (is_slli, inst[12], is_I_type);
  assign ImmSel = bit_extender_1_out | inst[6:4];  // OR_Gate or_1, 3 bits wide
  and and_5 (is_mulhu, inst[13], inst[14], inst[25], BSel);
  and and_6 (is_sra, inst[14], inst[12], inst[30], BSel);
  and and_7 (is_and, inst[12], inst[13], inst[14], BSel);
  and and_8 (is_srli, inst[14], inst[12], is_I_type);
  and and_9 (is_srai, inst[14], inst[12], is_I_type, inst[30]);
  and and_10 (is_andi, inst[12], inst[13], inst[14], is_I_type);
  // Probe on ImmSel
  and and_11 (is_sub, inst[30], BSel);
  and and_12 (is_xor, inst[14], BSel);
  and and_13 (is_slt, inst[13], BSel);
  and and_14 (is_or, inst[13], inst[14], BSel);
  and and_15 (is_slti, inst[13], is_I_type);
  and and_16 (is_ori, inst[13], inst[14], is_I_type);
  and and_17 (is_xori, inst[14], is_I_type);
  and and_18 (is_mul, inst[25], BSel);
  and and_19 (is_SB_or_is_jalr, inst[0], inst[1], inst[2], ~inst[3], ~inst[4], inst[5], inst[6]);  // AND_Gate
  and and_20 (is_UJ, inst[0], inst[1], inst[2], inst[3], ~inst[4], inst[5], inst[6]);  // AND_Gate
  or or_2 (in_4[1], is_mulhu, is_slt, is_or, is_and, is_slti, is_ori, is_andi, is_lui);
  or or_3 (in_4[2], is_sub, is_xor, is_srl, is_sra, is_or, is_and, is_xori, is_srli, is_srai, is_ori, is_andi, is_lui);
  or or_4 (in_4[3], is_mul, is_sub, is_mulh, is_mulhu, is_sra, is_srai, is_lui);
  or or_5 (PCSel, is_SB_or_is_jalr, is_UJ);
  or or_6 (or_6_out, MemRW, is_SB_or_is_jalr);
  not not_1 (RegWEn, or_6_out);
  or or_7 (in_4[0], is_sll, is_mulh, is_mulhu, is_srl, is_sra, is_and, is_slli, is_srli, is_srai, is_andi);
  and and_21 (and_21_out, inst[13], inst[14]);
  and and_22 (is_lui, inst[0], inst[1], inst[2], ~inst[3], inst[4], inst[5], ~inst[6]);  // AND_Gate
  and and_23 (is_UJ_type, inst[0], inst[1], inst[2], inst[3], ~inst[4], inst[5], inst[6]);  // AND_Gate
  and and_24 (BSel, inst[0], inst[1], ~inst[2], ~inst[3], inst[4], inst[5], ~inst[6]);  // AND_Gate
  and and_25 (MemRW, inst[0], inst[1], ~inst[2], ~inst[3], ~inst[4], inst[5], ~inst[6]);  // AND_Gate
  and and_26 (BrUn, is_SB_or_is_jalr, and_21_out);
  or or_8 (or_8_out, is_SB_or_is_jalr, is_UJ_type, is_lui);
  not not_2 (ASel, or_8_out);

  assign ALUSel = in_4;

  // Other names for the same wires on the sheet: opcode[6:0] = inst[6:0]; opcode_4 = inst[4]; opcode_5 = inst[5];
  //   opcode_6 = inst[6]; alu_xxx1 = in_4[0]; alu_xx1x = in_4[1]; alu_x1xx = in_4[2]; alu_1xxx = in_4[3];
  //   opcode_0 = inst[0]; opcode_1 = inst[1]; opcode_2 = inst[2]; opcode_3 = inst[3]; rd[4:0] = inst[11:7];
  //   funct3[2:0] = inst[14:12]; funct3_0 = inst[12]; funct3_1 = inst[13]; funct3_2 = inst[14];
  //   rs1[4:0] = inst[19:15]; imm[11:0] = inst[31:20]; rs2[4:0] = inst[24:20]; funct7[6:0] = inst[31:25];
  //   funct7_0 = inst[25]; immed[6:0] = inst[31:25]; funct7_1 = inst[26]; funct7_2 = inst[27]; funct7_3 = inst[28];
  //   funct7_4 = inst[29]; funct7_5 = inst[30]; funct7_6 = inst[31]; is_U_type = is_lui; is_R_type = BSel;
  //   is_S_type = MemRW; is_SB_type = is_SB_or_is_jalr

  // Notes on the sheet:
  //   I-type: 000,0011
  //   U-type: 001,0111
  //   S-type: 010,0011
  //   R-type: 011,0011; no imm
  //   SB-type: 110,0011
  //   UJ-type: 110,1111
  //   INPUTS to your circuit
  //   ImmSel generator logic
  //   while writting ImmSel, Rtype does not contain imm, so Rtype would not be included.
  //   there is another way to design this circuit, refer to cnblogs: 16225150 
  //   DON'T CHANGE THE LOCATIONS OF THE INPUTS AND OUTPUTS!
  //   OUTPUT from your circuit
  //   the rightest 2 bit always be 1 in these instruction, so this 2 bit would not be contained. becasue this 2 bit cannot identify instrcut type
  //   the highest(leftest) bits shows a regularity. Itype-> 000, Utype->001, Stype->010, SBType-> 110, UJType->110
  //   these 3bits cannot distinct UJ/SB type only, but the 3rd bit is 1 only in UJType. so we can make OR between highest 3bits and extended 3rd bit, to produce a regularity 3bits
  //   THIS CONTROL LOGIC CONTAINS HARD-WIRTED CIRCUIT, BECAUSE THIS PROJECT TEST FEW OF INSTRUCTIOS ONLY
  //   PCSel
  //   BrUn
endmodule
