// Logisim project cpu.circ as structural Verilog: 1 circuit, main circuit cpu
module cpu (
  input  clk,
  input  [31:0] INSTRUCTION,
  input  [31:0] READ_DATA,
  output [31:0] WRITE_ADDRESS,
  output [31:0] PROGRAM_COUNTER,
  output [31:0] ra,
  output [31:0] sp,
  output [31:0] t0,
  output [31:0] t1,
  output [31:0] t2,
  output [31:0] s0,
  output [31:0] s1,
  output [31:0] a0,
  output [31:0] tohost,
  output [3:0] WRITE_ENABLE,
  output [31:0] WRITE_DATA
);

  wire breq, brlt, brun, control_logic_1_bsel, control_logic_1_regwen, PCSel;
  wire [2:0] control_logic_1_immsel;
  wire [3:0] control_logic_1_alusel;
  wire [31:0] adder_1_out, aluresult, imm_gen_1_imm, multiplexer_1_out, multiplexer_2_out, rs1_data, rs2_data;

  Adder #(.width(32)) adder_1 (.a(PROGRAM_COUNTER), .b(32'h4), .out(adder_1_out));  // open: cin, cout
  Multiplexer #(.width(32)) multiplexer_1 (.in0(adder_1_out), .in1(aluresult), .out(multiplexer_1_out), .sel(PCSel));
  Register #(.width(32)) PC (.D(multiplexer_1_out), .clk(clk), .Q(PROGRAM_COUNTER));  // open: en, clr
  branch_comp branch_comp_1 (.rs1(rs1_data), .rs2(rs2_data), .BrUn(brun), .BrEq(breq), .BrLt(brlt));
  control_logic control_logic_1 (
    .PCSel(PCSel), .RegWEn(control_logic_1_regwen), .ImmSel(control_logic_1_immsel),
    .BSel(control_logic_1_bsel), .ALUSel(control_logic_1_alusel), .inst(INSTRUCTION));  // open: CSRWen, BrUn, ASel, MemRW, WBSel, CSRSel, BrEq, BrLt
  imm_gen imm_gen_1 (.inst(INSTRUCTION), .ImmSel(control_logic_1_immsel), .imm(imm_gen_1_imm));
  regfile regfile_1 (
    .rs1(INSTRUCTION[19:15]), .rs2(INSTRUCTION[24:20]), .rd(INSTRUCTION[11:7]), .Write_Data(aluresult),
    .RegWEn(control_logic_1_regwen), .clk(clk), .ra(ra), .sp(sp), .t0(t0), .t1(t1), .t2(t2), .s0(s0),
    .s1(s1), .a0(a0), .Read_Data_1(rs1_data), .Read_Data_2(rs2_data));
  Multiplexer #(.width(32)) multiplexer_2 (
    .in0(rs2_data), .in1(imm_gen_1_imm), .out(multiplexer_2_out), .sel(control_logic_1_bsel));
  alu alu_1 (
    .Result(aluresult), .A(rs1_data), .B(multiplexer_2_out), .ALUSel(control_logic_1_alusel));  // open: out_5, out_6
  csr csr_1 (.tohost(tohost));  // open: CSR_address, CSR_din, CSR_WE, clk

  // Other names for the same wires on the sheet: opcode[6:0] = INSTRUCTION[6:0]; rd[4:0] = INSTRUCTION[11:7];
  //   funct3[2:0] = INSTRUCTION[14:12]; rs1[4:0] = INSTRUCTION[19:15]; imm[11:0] = INSTRUCTION[31:20];
  //   rs2[4:0] = INSTRUCTION[24:20]; funct7[6:0] = INSTRUCTION[31:25]; immed[6:0] = INSTRUCTION[31:25]

  // Notes on the sheet:
  //   PCSel
  //   Output to IMEM
  //   IMEM (do **NOT** move this)
  //   Inputs from IMEM
  //   It is OK to move the PC, RegFile, ALU, MEM, Branch Comp, Imm Gen, and Control Logic to wherever is most convenient for you when constructing your CPU, and to delete this text
  //   Inputs/Outputs for testing. Do **NOT** move these.
  //   Outputs To DMEM
  //   DMEM (do **NOT** move this)
  //   Inputs From DMEM
endmodule
